# Fritzing sketch led_6channel_test (saved by Fritzing 0.8.3b)
breadboards: 1

parts:
  LED1 = LED - 5mm [color="Red (633nm)" package="5 mm [THT]"]
  LED2 = LED - 5mm [color="Red (633nm)" package="5 mm [THT]"]
  LED3 = LED - 5mm [color="Red (633nm)" package="5 mm [THT]"]
  LED4 = LED - 5mm [color="Red (633nm)" package="5 mm [THT]"]
  LED5 = LED - 5mm [color="Red (633nm)" package="5 mm [THT]"]
  LED6 = LED - 5mm [color="Red (633nm)" package="5 mm [THT]"]
  IC1 = ULN2803A [package=THT]
  BeagleBone1 = BeagleBone Black
  R2 = Resistor [tolerance=±5% resistance=120 package="1206 [SMD]"]
  R3 = Resistor [tolerance=±5% resistance=120 package="1206 [SMD]"]
  R4 = Resistor [tolerance=±5% resistance=120 package="1206 [SMD]"]
  R5 = Resistor [tolerance=±5% resistance=120 package="1206 [SMD]"]
  R8 = Resistor [tolerance=±5% resistance=120 package="1206 [SMD]"]
  R1 = Resistor [tolerance=±5% resistance=120 package="1206 [SMD]"]

nets (from the schematic view):
  N1: LED1.cathode, IC1.Out_1
  N2: LED1.anode, R1.Pin_1
  N3: LED2.cathode, IC1.Out_2
  N4: LED2.anode, R2.Pin_1
  N5: LED3.cathode, IC1.Out_3
  N6: LED3.anode, R3.Pin_1
  N7: LED4.cathode, IC1.Out_4
  N8: LED4.anode, R4.Pin_1
  N9: LED5.cathode, IC1.Out_5
  N10: LED5.anode, R5.Pin_1
  N11: LED6.cathode, IC1.Out_6
  N12: LED6.anode, R8.Pin_1
  N13: IC1.In_1, BeagleBone1.no_name_yet#14
  N14: IC1.In_2, BeagleBone1.no_name_yet#16
  N15: IC1.In_3, BeagleBone1.no_name_yet#21
  N16: IC1.In_4, BeagleBone1.no_name_yet#22
  N17: IC1.In_5, BeagleBone1.no_name_yet#113
  N18: IC1.In_6, BeagleBone1.no_name_yet#119
  GND: IC1.0V, BeagleBone1.no_name_yet#1
  5V: IC1.COM_-_Common, BeagleBone1.no_name_yet#5, R2.Pin_0, R3.Pin_0, R4.Pin_0, R5.Pin_0, R8.Pin_0, R1.Pin_0

custom parts:
  BeagleBone Black: BeagleBone Black rev. A5B
