# Fritzing sketch orfi_twitter (saved by Fritzing 0.8.3b)
breadboards: 1

parts:
  ISP1 = shrouded pin header, 16 pins [form="♂ (shrouded male)"]
  S1 = Pushbutton [part_number="left side" package="[THT]"]
  S2 = Pushbutton [part_number="right side" package="[THT]"]
  LED1 = LED - 5mm [color="Red (633nm)" part_number="left inner" package="5 mm [THT]"]
  LED2 = LED - 5mm [color="Red (633nm)" part_number="left outer" package="5 mm [THT]"]
  LED3 = LED - 5mm [color="Red (633nm)" part_number="middle top" package="5 mm [THT]"]
  LED4 = LED - 5mm [color="Red (633nm)" part_number="middle bottom" package="5 mm [THT]"]
  LED5 = LED - 5mm [color="Red (633nm)" part_number="right inner" package="5 mm [THT]"]
  LED6 = LED - 5mm [color="Red (633nm)" part_number="right outer" package="5 mm [THT]"]
  IC1 = ULN2803A [package=THT]
  BeagleBone1 = BeagleBone Black
  ISP2 = shrouded pin header, 16 pins [form="♂ (shrouded male)"]
  R2 = Resistor [tolerance=±5% resistance=120 package="1206 [SMD]"]
  R3 = Resistor [tolerance=±5% resistance=120 package="1206 [SMD]"]
  R4 = Resistor [tolerance=±5% resistance=120 package="1206 [SMD]"]
  R5 = Resistor [tolerance=±5% resistance=120 package="1206 [SMD]"]
  R8 = Resistor [tolerance=±5% resistance=120 package="1206 [SMD]"]
  R1 = Resistor [tolerance=±5% resistance=120 package="1206 [SMD]"]
  S3 = Pushbutton [part_number="off button" package="[THT]"]

nets (from the schematic view):
  N1: ISP1.pin1, S1.Pin_1, S1.Pin_2
  N2: ISP1.pin2, S1.Pin_3, S1.Pin_4
  N3: ISP1.pin3, LED1.cathode
  N4: ISP1.pin4, LED1.anode
  N5: ISP1.pin5, LED2.cathode
  N6: ISP1.pin6, LED2.anode
  N7: ISP1.pin7, LED3.cathode
  N8: ISP1.pin8, LED3.anode
  N9: ISP1.pin9, LED4.cathode
  N10: ISP1.pin10, LED4.anode
  N11: ISP1.pin11, LED5.cathode
  N12: ISP1.pin12, LED5.anode
  N13: ISP1.pin13, LED6.cathode
  N14: ISP1.pin14, LED6.anode
  N15: ISP1.pin15, S2.Pin_1, S2.Pin_2
  N16: ISP1.pin16, S2.Pin_3, S2.Pin_4
  N17: IC1.In_1, BeagleBone1.no_name_yet#14
  N18: IC1.In_2, BeagleBone1.no_name_yet#16
  N19: IC1.In_3, BeagleBone1.no_name_yet#21
  N20: IC1.In_4, BeagleBone1.no_name_yet#22
  N21: IC1.In_5, BeagleBone1.no_name_yet#113
  N22: IC1.In_6, BeagleBone1.no_name_yet#119
  GND: IC1.0V, BeagleBone1.no_name_yet#1
  5V: IC1.COM_-_Common, BeagleBone1.no_name_yet#5, R2.Pin_0, R3.Pin_0, R4.Pin_0, R5.Pin_0, R8.Pin_0, R1.Pin_0
  N23: IC1.Out_6, ISP2.pin13
  N24: IC1.Out_5, ISP2.pin11
  N25: IC1.Out_4, ISP2.pin9
  N26: IC1.Out_3, ISP2.pin7
  N27: IC1.Out_2, ISP2.pin5
  N28: IC1.Out_1, ISP2.pin3
  3.3V: BeagleBone1.no_name_yet#3, ISP2.pin1, ISP2.pin15, S3.Pin_1, S3.Pin_2
  N29: BeagleBone1.no_name_yet#23, S3.Pin_3, S3.Pin_4
  N30: BeagleBone1.no_name_yet#27, ISP2.pin2
  N31: BeagleBone1.no_name_yet#30, ISP2.pin16
  N32: ISP2.pin4, R1.Pin_1
  N33: ISP2.pin6, R2.Pin_1
  N34: ISP2.pin8, R3.Pin_1
  N35: ISP2.pin10, R4.Pin_1
  N36: ISP2.pin12, R5.Pin_1
  N37: ISP2.pin14, R8.Pin_1

custom parts:
  BeagleBone Black: BeagleBone Black rev. A5B
